// Logisim project PROJECT 332 Recent version.circ as structural Verilog
module NOT_IC_7404 (
  input  vcc,
  input  in_2,
  input  in_3,
  input  in_4,
  input  in_5,
  input  in_6,
  output GND,
  output out_8,
  output out_9,
  output out_10,
  output out_11,
  output out_12
);

  not not_1 (GND, vcc);
  not not_2 (out_8, in_2);
  not not_3 (out_9, in_3);
  not not_4 (out_10, in_4);
  not not_5 (out_11, in_5);
  not not_6 (out_12, in_6);
endmodule

module AND_IC_7408 (
  input  in_1,
  input  in_2,
  input  in_3,
  input  in_4,
  input  in_5,
  input  in_6,
  input  in_7,
  input  in_8,
  output out_9,
  output out_10,
  output out_11,
  output out_12
);

  and and_1 (out_9, in_1, in_2);
  and and_2 (out_10, in_3, in_4);
  and and_3 (out_11, in_5, in_6);
  and and_4 (out_12, in_7, in_8);

  // Notes on the sheet:
  //   VCC
  //   GND
endmodule

module OR__IC_7432 (
  input  in_1,
  input  in_2,
  input  in_3,
  input  in_4,
  input  in_5,
  input  in_6,
  input  in_7,
  input  in_8,
  output out_9,
  output out_10,
  output out_11,
  output out_12
);

  or or_1 (out_9, in_1, in_2);
  or or_2 (out_10, in_3, in_4);
  or or_3 (out_11, in_5, in_6);
  or or_4 (out_12, in_7, in_8);
endmodule

module XOR (
  input  in_1,
  input  in_2,
  input  in_3,
  input  in_4,
  input  in_5,
  input  in_6,
  input  in_7,
  input  in_8,
  output out_9,
  output out_10,
  output out_11,
  output out_12
);

  xor xor_1 (out_9, in_1, in_2);
  xor xor_2 (out_10, in_3, in_4);
  xor xor_3 (out_11, in_5, in_6);
  xor xor_4 (out_12, in_7, in_8);
endmodule

module MUX__IC_74LS153 (
  input  s2,
  input  S1,
  input  A,
  input  B,
  input  C,
  input  D,
  input  Ea,
  input  A_2,
  input  B_2,
  input  C_2,
  input  D_2,
  input  Eb,
  output out_13,
  output circuit_b
);

  wire and_1_out, and_2_out, and_3_out, and_4_out, and_5_out, and_6_out, and_7_out, and_8_out, not_1_out,
       not_2_out, not_3_out, not_4_out, not_5_out, not_6_out;

  not not_1 (not_1_out, s2);
  not not_2 (not_2_out, S1);
  not not_3 (not_3_out, Ea);
  not not_4 (not_4_out, s2);
  not not_5 (not_5_out, S1);
  not not_6 (not_6_out, Eb);
  and and_1 (and_1_out, A, not_2_out, not_1_out, not_3_out);
  and and_2 (and_2_out, B, not_2_out, s2, s2, not_3_out);
  and and_3 (and_3_out, C, S1, not_3_out, not_1_out);
  and and_4 (and_4_out, D, S1, s2, not_3_out);
  and and_5 (and_5_out, A_2, not_5_out, not_4_out, not_6_out);
  and and_6 (and_6_out, B_2, not_5_out, s2, s2, not_6_out);
  and and_7 (and_7_out, C_2, S1, not_6_out, not_4_out);
  and and_8 (and_8_out, D_2, S1, s2, not_6_out);
  or or_1 (out_13, and_1_out, and_2_out, and_3_out, and_4_out);
  or or_2 (circuit_b, and_5_out, and_6_out, and_7_out, and_8_out);

  // Notes on the sheet:
  //   circuit a 
endmodule

module _2_BIT_ADDER (
  input  Ea,
  input  S2,
  input  S1,
  input  A1,
  input  B1,
  input  A2,
  input  B2,
  input  Eb,
  output out_9,
  output out_10
);

  wire and_ic_7408_1_out_9, and_ic_7408_1_out_10, not_ic_7404_1_gnd, not_ic_7404_1_out_9, or_ic_7432_1_out_9,
       or_ic_7432_1_out_10, xor_1_out_9, xor_1_out_10;

  AND_IC_7408 and_ic_7408_1 (
    .in_2(B1), .in_4(B2), .out_9(and_ic_7408_1_out_9), .out_10(and_ic_7408_1_out_10), .in_3(A2), .in_1(A1));  // open: in_6, in_8, out_11, out_12, in_5, in_7
  OR__IC_7432 or_ic_7432_1 (
    .in_1(A1), .in_2(B1), .in_3(A2), .in_4(B2), .out_9(or_ic_7432_1_out_9), .out_10(or_ic_7432_1_out_10));  // open: in_5, in_6, in_7, in_8, out_11, out_12
  XOR xor_1 (
    .in_1(A1), .in_2(B1), .in_3(A2), .in_4(B2), .out_9(xor_1_out_9), .out_10(xor_1_out_10));  // open: in_5, in_6, in_7, in_8, out_11, out_12
  NOT_IC_7404 not_ic_7404_1 (
    .vcc(A1), .in_3(A2), .GND(not_ic_7404_1_gnd), .out_9(not_ic_7404_1_out_9));  // open: in_2, in_4, in_5, in_6, out_8, out_10, out_11, out_12
  MUX__IC_74LS153 mux_ic_74ls153_1 (
    .s2(S2), .S1(S1), .A(and_ic_7408_1_out_10), .B(or_ic_7432_1_out_10), .C(xor_1_out_10),
    .D(not_ic_7404_1_out_9), .out_13(out_10), .A_2(and_ic_7408_1_out_9), .B_2(or_ic_7432_1_out_9),
    .circuit_b(out_9), .C_2(xor_1_out_9), .D_2(not_ic_7404_1_gnd), .Ea(Ea), .Eb(Eb));
endmodule

module _4_bit_adder (
  input  in_1,
  input  in_2,
  input  in_3,
  input  in_4,
  input  in_5,
  input  in_6,
  input  in_7,
  input  in_8,
  input  in_9,
  output out_10,
  output out_11,
  output out_12,
  output out_13,
  output out_14
);

  wire and_1_out, and_2_out, and_3_out, and_4_out, and_5_out, and_6_out, and_7_out, and_8_out, or_1_out,
       or_2_out, or_3_out, xor_1_out, xor_2_out, xor_3_out, xor_4_out;

  xor xor_1 (xor_1_out, in_1, in_2);
  and and_1 (and_1_out, in_1, in_2);
  xor xor_2 (xor_2_out, in_4, in_5);
  and and_2 (and_2_out, in_4, in_5);
  xor xor_3 (xor_3_out, in_6, in_7);
  and and_3 (and_3_out, in_6, in_7);
  xor xor_4 (xor_4_out, in_8, in_9);
  and and_4 (and_4_out, in_8, in_9);
  xor xor_5 (out_10, xor_1_out, in_3);
  and and_5 (and_5_out, xor_1_out, in_3);
  xor xor_6 (out_11, xor_2_out, or_1_out);
  and and_6 (and_6_out, xor_2_out, or_1_out);
  xor xor_7 (out_12, xor_3_out, or_2_out);
  and and_7 (and_7_out, xor_3_out, or_2_out);
  xor xor_8 (out_13, xor_4_out, or_3_out);
  and and_8 (and_8_out, xor_4_out, or_3_out);
  or or_1 (or_1_out, and_5_out, and_1_out);
  or or_2 (or_2_out, and_6_out, and_2_out);
  or or_3 (or_3_out, and_7_out, and_3_out);
  or or_4 (out_14, and_8_out, and_4_out);
endmodule

module _4_bit_multiplier (
  input  A4,
  input  A3,
  input  A2,
  input  A1,
  input  B4,
  input  B3,
  input  B2,
  input  B1,
  input  in_9,
  output S1,
  output S2,
  output S3,
  output S4,
  output S5,
  output S6,
  output S7,
  output S8
);

  wire and_ic_7408_1_out_9, and_ic_7408_1_out_10, and_ic_7408_1_out_11, and_ic_7408_2_out_9,
       and_ic_7408_2_out_10, and_ic_7408_2_out_11, and_ic_7408_2_out_12, and_ic_7408_3_out_9,
       and_ic_7408_3_out_10, and_ic_7408_3_out_11, and_ic_7408_3_out_12, and_ic_7408_4_out_9,
       and_ic_7408_4_out_10, and_ic_7408_4_out_11, and_ic_7408_4_out_12, n4_bit_adder_1_out_11,
       n4_bit_adder_1_out_12, n4_bit_adder_1_out_13, n4_bit_adder_1_out_14, n4_bit_adder_2_out_11,
       n4_bit_adder_2_out_12, n4_bit_adder_2_out_13, n4_bit_adder_2_out_14;

  AND_IC_7408 and_ic_7408_1 (
    .in_2(A1), .in_4(B3), .in_6(A1), .in_8(B1), .out_9(and_ic_7408_1_out_9), .out_10(and_ic_7408_1_out_10),
    .out_11(and_ic_7408_1_out_11), .out_12(S1), .in_3(A1), .in_1(B4), .in_5(B2), .in_7(A1));
  AND_IC_7408 and_ic_7408_2 (
    .in_2(A2), .in_4(B3), .in_6(A2), .in_8(B1), .out_9(and_ic_7408_2_out_9), .out_10(and_ic_7408_2_out_10),
    .out_11(and_ic_7408_2_out_11), .out_12(and_ic_7408_2_out_12), .in_3(A2), .in_1(B4), .in_5(B2), .in_7(A2));
  AND_IC_7408 and_ic_7408_3 (
    .in_2(A3), .in_4(B3), .in_6(A3), .in_8(B1), .out_9(and_ic_7408_3_out_9), .out_10(and_ic_7408_3_out_10),
    .out_11(and_ic_7408_3_out_11), .out_12(and_ic_7408_3_out_12), .in_3(A3), .in_1(B4), .in_5(B2), .in_7(A3));
  AND_IC_7408 and_ic_7408_4 (
    .in_2(A4), .in_4(B3), .in_6(A4), .in_8(B1), .out_9(and_ic_7408_4_out_9), .out_10(and_ic_7408_4_out_10),
    .out_11(and_ic_7408_4_out_11), .out_12(and_ic_7408_4_out_12), .in_3(A4), .in_1(B4), .in_5(B2), .in_7(A4));
  _4_bit_adder u_4_bit_adder_1 (
    .in_1(and_ic_7408_1_out_11), .in_2(and_ic_7408_2_out_12), .in_3(1'b0), .in_4(and_ic_7408_1_out_10),
    .in_5(and_ic_7408_2_out_11), .in_6(and_ic_7408_1_out_9), .in_7(and_ic_7408_2_out_10), .in_8(in_9),
    .in_9(and_ic_7408_2_out_9), .out_10(S2), .out_11(n4_bit_adder_1_out_11), .out_12(n4_bit_adder_1_out_12),
    .out_13(n4_bit_adder_1_out_13), .out_14(n4_bit_adder_1_out_14));
  _4_bit_adder u_4_bit_adder_2 (
    .in_1(n4_bit_adder_1_out_11), .in_2(and_ic_7408_3_out_12), .in_3(in_9), .in_4(n4_bit_adder_1_out_12),
    .in_5(and_ic_7408_3_out_11), .in_6(n4_bit_adder_1_out_13), .in_7(and_ic_7408_3_out_10),
    .in_8(n4_bit_adder_1_out_14), .in_9(and_ic_7408_3_out_9), .out_10(S3), .out_11(n4_bit_adder_2_out_11),
    .out_12(n4_bit_adder_2_out_12), .out_13(n4_bit_adder_2_out_13), .out_14(n4_bit_adder_2_out_14));
  _4_bit_adder u_4_bit_adder_3 (
    .in_1(n4_bit_adder_2_out_11), .in_2(and_ic_7408_4_out_12), .in_3(in_9), .in_4(n4_bit_adder_2_out_12),
    .in_5(and_ic_7408_4_out_11), .in_6(n4_bit_adder_2_out_13), .in_7(and_ic_7408_4_out_10),
    .in_8(n4_bit_adder_2_out_14), .in_9(and_ic_7408_4_out_9), .out_10(S4), .out_11(S5), .out_12(S6),
    .out_13(S7), .out_14(S8));
endmodule

module Up_Down_Counter (
);

  AND_IC_7408 and_ic_7408_1 ();  // open: in_2, in_4, in_6, in_8, out_9, out_10, out_11, out_12, in_3, in_1, in_5, in_7
  XOR xor_1 ();  // open: in_1, in_2, in_3, in_4, in_5, in_6, in_7, in_8, out_9, out_10, out_11, out_12
  OR__IC_7432 or_ic_7432_1 ();  // open: in_1, in_2, in_3, in_4, in_5, in_6, in_7, in_8, out_9, out_10, out_11, out_12
endmodule

module D_flip_flop__IC_74LS74 (
  input  set,
  input  clock,
  input  data,
  input  reset,
  input  set_2,
  input  clock_2,
  input  data_2,
  input  reset_2,
  output Q,
  output Q_prime,
  output Q_2,
  output Q_prime_2
);

  wire nand_1_out, nand_2_out, nand_3_out, nand_4_out, nand_5_out, nand_6_out, nand_7_out, nand_8_out,
       not_1_out, not_2_out;

  not not_1 (not_1_out, set);
  not not_2 (not_2_out, set_2);
  nand nand_1 (nand_1_out, not_1_out, nand_4_out, nand_2_out);
  nand nand_2 (nand_2_out, nand_1_out, clock, reset);
  nand nand_3 (nand_3_out, nand_4_out, nand_2_out, clock);
  nand nand_4 (nand_4_out, nand_3_out, data, reset);
  nand nand_5 (nand_5_out, nand_8_out, clock_2, reset_2);
  nand nand_6 (nand_6_out, nand_7_out, nand_5_out, clock_2);
  nand nand_7 (nand_7_out, nand_6_out, data_2, reset_2);
  nand nand_8 (nand_8_out, not_2_out, nand_7_out, nand_5_out);
  nand nand_9 (Q, not_1_out, nand_2_out, Q_prime);
  nand nand_10 (Q_prime, Q, nand_3_out, reset);
  nand nand_11 (Q_2, not_2_out, nand_5_out, Q_prime_2);
  nand nand_12 (Q_prime_2, Q_2, nand_6_out, reset_2);
endmodule

module _4_BIT_BINARY_UP_DOWN_COUNTER (
  input  E,
  input  Reset,
  input  Down,
  input  Up,
  output D,
  output C,
  output B,
  output A
);

  wire _1_out_9, _1_out_10, _1_out_11, and_ic_7408_1_out_9, and_ic_7408_1_out_10, and_ic_7408_1_out_11,
       and_ic_7408_1_out_12, clock_1_out, d_flip_flop_ic_74ls74_1_q_prime, not_ic_7404_1_gnd,
       or_ic_7432_1_out_9, or_ic_7432_1_out_10, or_ic_7432_1_out_11, or_ic_7432_1_out_12, s_q_prime,
       s_q_prime_2, xor_1_out_9, xor_1_out_10, xor_1_out_11, xor_1_out_12;

  Clock clock_1 (.out(clock_1_out));
  NOT_IC_7404 not_ic_7404_1 (
    .vcc(Up), .GND(not_ic_7404_1_gnd));  // open: in_2, in_3, in_4, in_5, in_6, out_8, out_9, out_10, out_11, out_12
  AND_IC_7408 and_ic_7408_1 (
    .in_2(_1_out_11), .in_4(_1_out_10), .in_6(B), .in_8(d_flip_flop_ic_74ls74_1_q_prime),
    .out_9(and_ic_7408_1_out_9), .out_10(and_ic_7408_1_out_10), .out_11(and_ic_7408_1_out_11),
    .out_12(and_ic_7408_1_out_12), .in_3(s_q_prime_2), .in_1(C), .in_5(and_ic_7408_1_out_9),
    .in_7(and_ic_7408_1_out_10));
  AND_IC_7408 _1 (
    .in_2(Down), .in_4(s_q_prime), .in_6(D), .out_9(_1_out_9), .out_10(_1_out_10), .out_11(_1_out_11),
    .in_3(_1_out_9), .in_1(not_ic_7404_1_gnd), .in_5(Up));  // open: in_8, out_12, in_7
  OR__IC_7432 or_ic_7432_1 (
    .in_1(Up), .in_2(_1_out_9), .in_3(_1_out_11), .in_4(_1_out_10), .in_5(and_ic_7408_1_out_12),
    .in_6(and_ic_7408_1_out_11), .in_7(and_ic_7408_1_out_10), .in_8(and_ic_7408_1_out_9),
    .out_9(or_ic_7432_1_out_9), .out_10(or_ic_7432_1_out_10), .out_11(or_ic_7432_1_out_11),
    .out_12(or_ic_7432_1_out_12));
  XOR xor_1 (
    .in_1(D), .in_2(or_ic_7432_1_out_9), .in_3(or_ic_7432_1_out_10), .in_4(C), .in_5(or_ic_7432_1_out_11),
    .in_6(A), .in_7(B), .in_8(or_ic_7432_1_out_12), .out_9(xor_1_out_9), .out_10(xor_1_out_10),
    .out_11(xor_1_out_11), .out_12(xor_1_out_12));
  D_flip_flop__IC_74LS74 s (
    .set(E), .data(xor_1_out_9), .reset(Reset), .Q(D), .Q_prime(s_q_prime), .set_2(E), .Q_2(C),
    .Q_prime_2(s_q_prime_2), .data_2(xor_1_out_10), .reset_2(Reset), .clock(clock_1_out),
    .clock_2(clock_1_out));
  D_flip_flop__IC_74LS74 d_flip_flop_ic_74ls74_1 (
    .set(E), .data(xor_1_out_12), .reset(Reset), .Q(B), .Q_prime(d_flip_flop_ic_74ls74_1_q_prime), .set_2(E),
    .Q_2(A), .data_2(xor_1_out_11), .reset_2(Reset), .clock(clock_1_out), .clock_2(clock_1_out));  // open: Q_prime_2

  // Notes on the sheet:
  //   4
  //   5
  //   1
  //   2
  //   6
  //   7
  //   3
  //   S2
endmodule

module Register_File (
  input  [11:0] in_1,
  input  in_2,
  input  [2:0] in_3,
  input  [2:0] in_4,
  input  [2:0] in_5,
  input  in_6,
  output [11:0] out_7,
  output [11:0] out_8
);

  wire demultiplexer_1_out0, demultiplexer_1_out1, demultiplexer_1_out2, demultiplexer_1_out3,
       demultiplexer_1_out4, demultiplexer_1_out5, demultiplexer_1_out6, demultiplexer_1_out7;
  wire [11:0] register_1_q, register_2_q, register_3_q, register_4_q, register_5_q, register_6_q,
       register_7_q, register_8_q;

  Demultiplexer #(.select(3), .enable("false")) demultiplexer_1 (
    .out0(demultiplexer_1_out0), .out1(demultiplexer_1_out1), .out2(demultiplexer_1_out2),
    .out3(demultiplexer_1_out3), .out4(demultiplexer_1_out4), .out5(demultiplexer_1_out5),
    .out6(demultiplexer_1_out6), .out7(demultiplexer_1_out7), .in(in_2), .sel(in_5));
  Register #(.width(12)) register_1 (.D(in_1), .en(demultiplexer_1_out0), .Q(register_1_q), .clk(in_6));  // open: clr
  Register #(.width(12)) register_2 (.D(in_1), .en(demultiplexer_1_out1), .Q(register_2_q), .clk(in_6));  // open: clr
  Register #(.width(12)) register_3 (.D(in_1), .en(demultiplexer_1_out2), .Q(register_3_q), .clk(in_6));  // open: clr
  Register #(.width(12)) register_4 (.D(in_1), .en(demultiplexer_1_out3), .Q(register_4_q), .clk(in_6));  // open: clr
  Register #(.width(12)) register_5 (.D(in_1), .en(demultiplexer_1_out4), .Q(register_5_q), .clk(in_6));  // open: clr
  Register #(.width(12)) register_6 (.D(in_1), .en(demultiplexer_1_out5), .Q(register_6_q), .clk(in_6));  // open: clr
  Register #(.width(12)) register_7 (.D(in_1), .en(demultiplexer_1_out6), .Q(register_7_q), .clk(in_6));  // open: clr
  Register #(.width(12)) register_8 (.D(in_1), .en(demultiplexer_1_out7), .Q(register_8_q), .clk(in_6));  // open: clr
  Multiplexer #(.select(3), .width(12), .enable("false")) multiplexer_1 (
    .in0(register_1_q), .in1(register_2_q), .in2(register_3_q), .in3(register_4_q), .in4(register_5_q),
    .in5(register_6_q), .in6(register_7_q), .in7(register_8_q), .out(out_7), .sel(in_3));
  Multiplexer #(.select(3), .width(12), .enable("false")) multiplexer_2 (
    .in0(register_1_q), .in1(register_2_q), .in2(register_3_q), .in3(register_4_q), .in4(register_5_q),
    .in5(register_6_q), .in6(register_7_q), .in7(register_8_q), .out(out_8), .sel(in_4));
endmodule

module ALU__1_bit (
  input  A,
  input  B,
  input  C_in,
  input  B_invert,
  input  [1:0] Alu_op,
  output Result,
  output C_out
);

  wire adder_1_out, and_1_out, multiplexer_1_out, not_1_out, or_1_out, xor_1_out;

  not not_1 (not_1_out, B);
  Multiplexer multiplexer_1 (.in0(B), .in1(not_1_out), .out(multiplexer_1_out), .sel(B_invert));  // open: en
  and and_1 (and_1_out, A, multiplexer_1_out);
  or or_1 (or_1_out, A, multiplexer_1_out);
  xor xor_1 (xor_1_out, A, multiplexer_1_out);
  Adder #(.width(1)) adder_1 (.a(A), .b(multiplexer_1_out), .out(adder_1_out), .cin(C_in), .cout(C_out));
  Multiplexer #(.select(2)) multiplexer_2 (
    .in0(and_1_out), .in1(or_1_out), .in2(adder_1_out), .in3(xor_1_out), .out(Result), .sel(Alu_op));  // open: en
endmodule

module ALU_12_BIT (
  input  in_1,
  input  in_2,
  input  [1:0] in_3,
  input  [11:0] in_4,
  input  [11:0] in_5,
  output [11:0] out_6,
  output out_7
);

  wire alu_1_bit_1_c_out, alu_1_bit_2_c_out, alu_1_bit_3_c_out, alu_1_bit_4_c_out, alu_1_bit_5_c_out,
       alu_1_bit_6_c_out, alu_1_bit_7_c_out, alu_1_bit_8_c_out, alu_1_bit_9_c_out, alu_1_bit_10_c_out,
       alu_1_bit_11_c_out;

  ALU__1_bit alu_1_bit_1 (
    .A(in_4[0]), .B(in_5[0]), .B_invert(in_2), .C_in(in_1), .Result(out_6[0]), .Alu_op(in_3),
    .C_out(alu_1_bit_1_c_out));
  ALU__1_bit alu_1_bit_2 (
    .A(in_4[1]), .B(in_5[1]), .B_invert(in_2), .C_in(alu_1_bit_1_c_out), .Result(out_6[1]), .Alu_op(in_3),
    .C_out(alu_1_bit_2_c_out));
  ALU__1_bit alu_1_bit_3 (
    .A(in_4[2]), .B(in_5[2]), .B_invert(in_2), .C_in(alu_1_bit_2_c_out), .Result(out_6[2]), .Alu_op(in_3),
    .C_out(alu_1_bit_3_c_out));
  ALU__1_bit alu_1_bit_4 (
    .A(in_4[3]), .B(in_5[3]), .B_invert(in_2), .C_in(alu_1_bit_3_c_out), .Result(out_6[3]), .Alu_op(in_3),
    .C_out(alu_1_bit_4_c_out));
  ALU__1_bit alu_1_bit_5 (
    .A(in_4[4]), .B(in_5[4]), .B_invert(in_2), .C_in(alu_1_bit_4_c_out), .Result(out_6[4]), .Alu_op(in_3),
    .C_out(alu_1_bit_5_c_out));
  ALU__1_bit alu_1_bit_6 (
    .A(in_4[5]), .B(in_5[5]), .B_invert(in_2), .C_in(alu_1_bit_5_c_out), .Result(out_6[5]), .Alu_op(in_3),
    .C_out(alu_1_bit_6_c_out));
  ALU__1_bit alu_1_bit_7 (
    .A(in_4[6]), .B(in_5[6]), .B_invert(in_2), .C_in(alu_1_bit_6_c_out), .Result(out_6[6]), .Alu_op(in_3),
    .C_out(alu_1_bit_7_c_out));
  ALU__1_bit alu_1_bit_8 (
    .A(in_4[7]), .B(in_5[7]), .B_invert(in_2), .C_in(alu_1_bit_7_c_out), .Result(out_6[7]), .Alu_op(in_3),
    .C_out(alu_1_bit_8_c_out));
  ALU__1_bit alu_1_bit_9 (
    .A(in_4[8]), .B(in_5[8]), .B_invert(in_2), .C_in(alu_1_bit_8_c_out), .Result(out_6[8]), .Alu_op(in_3),
    .C_out(alu_1_bit_9_c_out));
  ALU__1_bit alu_1_bit_10 (
    .A(in_4[9]), .B(in_5[9]), .B_invert(in_2), .C_in(alu_1_bit_9_c_out), .Result(out_6[9]), .Alu_op(in_3),
    .C_out(alu_1_bit_10_c_out));
  ALU__1_bit alu_1_bit_11 (
    .A(in_4[10]), .B(in_5[10]), .B_invert(in_2), .C_in(alu_1_bit_10_c_out), .Result(out_6[10]),
    .Alu_op(in_3), .C_out(alu_1_bit_11_c_out));
  ALU__1_bit alu_1_bit_12 (
    .A(in_4[11]), .B(in_5[11]), .B_invert(in_2), .C_in(alu_1_bit_11_c_out), .Result(out_6[11]),
    .Alu_op(in_3), .C_out(out_7));
endmodule

module Datapath (
  input  [2:0] Opcode,
  output [11:0] out_2,
  output [2:0] Opcode_2,
  output [8:0] out_4,
  output [11:0] out_5,
  output [11:0] out_6,
  output [11:0] out_7,
  output [11:0] out_8,
  output [2:0] Opcode_3,
  output [2:0] RS,
  output [2:0] RT,
  output [2:0] out_12,
  output [11:0] out_13
);

  wire clock_1_out, control_unit_1_alu_src, control_unit_1_jump, control_unit_1_le_enb,
       control_unit_1_ram_to_reg, control_unit_1_regdst, control_unit_1_sub, control_unit_1_sw_enb,
       control_unit_1_wren;
  wire [1:0] control_unit_1_out_5;
  wire [2:0] multiplexer_2_out;
  wire [11:0] alu_12_bit_1_out_6, bit_extender_1_out, counter_1_q, multiplexer_1_out, ram_1_data;

  Multiplexer #(.width(12), .enable("false")) multiplexer_1 (
    .in0({out_2[11:9], out_5[8:0]}), .in1(out_2), .out(multiplexer_1_out), .sel(control_unit_1_jump));
  control_unit control_unit_1 (
    .in_1(Opcode), .RegDst(control_unit_1_regdst), .WrEn(control_unit_1_wren),
    .Alu_Src(control_unit_1_alu_src), .out_5(control_unit_1_out_5), .Sub(control_unit_1_sub),
    .le_enb(control_unit_1_le_enb), .sw_enb(control_unit_1_sw_enb), .RAM_to_Reg(control_unit_1_ram_to_reg),
    .Jump(control_unit_1_jump));
  Counter #(.width(12), .max('hfff)) counter_1 (
    .D(multiplexer_1_out), .Q(counter_1_q), .clk(clock_1_out));  // open: load, count, carry, clr
  Clock clock_1 (.out(clock_1_out));
  Adder #(.width(12)) adder_1 (.a(counter_1_q), .b(12'h1), .out({out_2[11:9], out_5[8:0]}));  // open: cin, cout
  ROM #(.addrWidth(12), .dataWidth(12)) rom_1 (.addr(counter_1_q), .data({Opcode_2, out_2[8:0]}));  // open: sel
  Multiplexer #(.width(3), .enable("false")) multiplexer_2 (
    .in0(out_2[2:0]), .in1(out_2[5:3]), .out(multiplexer_2_out), .sel(control_unit_1_regdst));
  Register_File u_RS (
    .in_1(out_8), .in_3(out_2[8:6]), .in_4(out_2[5:3]), .in_6(clock_1_out), .out_7(out_6), .out_8(out_13),
    .in_5(multiplexer_2_out), .in_2(control_unit_1_wren));
  assign bit_extender_1_out = {{9{1'b0}}, out_2[2:0]};  // Bit_Extender bit_extender_1
  Multiplexer #(.width(12), .enable("false")) multiplexer_3 (
    .in0(out_13), .in1(bit_extender_1_out), .out(out_7), .sel(control_unit_1_alu_src));
  ALU_12_BIT alu_12_bit_1 (
    .in_3(control_unit_1_out_5), .in_4(out_6), .in_5(out_7), .in_1(control_unit_1_sub),
    .in_2(control_unit_1_sub), .out_6(alu_12_bit_1_out_6));  // open: out_7
  RAM #(.addrWidth(12), .dataWidth(12), .bus("separate")) ram_1 (
    .addr(alu_12_bit_1_out_6), .din(out_13), .data(ram_1_data), .str(control_unit_1_sw_enb),
    .clk(clock_1_out), .ld(control_unit_1_le_enb));  // open: sel, clr
  Multiplexer #(.width(12), .enable("false")) multiplexer_4 (
    .in0(alu_12_bit_1_out_6), .in1(ram_1_data), .out(out_8), .sel(control_unit_1_ram_to_reg));

  assign Opcode_3 = Opcode_2;
  assign out_4 = out_2[8:0];
  assign out_5[11:9] = out_2[11:9];
  assign out_12 = out_2[2:0];
  assign RS = out_2[8:6];
  assign RT = out_2[5:3];

  // Notes on the sheet:
  //   Clock
  //   Reg_Dst
  //   Write_enb
  //   ALU_OP
  //   ALU_Src
  //   Sub
  //   Store_enb
  //   Load_enb
  //   RAM_to_Reg
  //   Jump
  //   Next-Instruction
  //   Instruction Memory (ROM)
  //   contents of rom_1 (hex, n*v repeats v):
  //   453
  //   Jump/Target
  //   Write Register
  //   Jump-Address
  //   Binv
  //   Data 1
  //   Data 2
  //   Data_for_store
  //   RAM
  //   Result_val
endmodule

module control_unit (
  input  [2:0] in_1,
  output RegDst,
  output WrEn,
  output Alu_Src,
  output [1:0] out_5,
  output Sub,
  output le_enb,
  output sw_enb,
  output RAM_to_Reg,
  output Jump
);

  wire and_3_out, and_4_out, and_5_out, not_1_out, not_2_out, not_3_out, not_4_out, not_5_out, not_6_out,
       not_7_out, not_8_out, not_9_out, not_10_out, not_11_out, not_12_out, not_13_out, not_14_out,
       not_15_out, not_16_out;

  not not_1 (not_1_out, in_1[0]);
  not not_2 (not_2_out, in_1[2]);
  not not_3 (not_3_out, in_1[1]);
  not not_4 (not_4_out, in_1[0]);
  not not_5 (not_5_out, in_1[2]);
  not not_6 (not_6_out, in_1[0]);
  not not_7 (not_7_out, in_1[0]);
  not not_8 (not_8_out, in_1[1]);
  not not_9 (not_9_out, in_1[2]);
  not not_10 (not_10_out, in_1[1]);
  not not_11 (not_11_out, in_1[2]);
  not not_12 (not_12_out, in_1[0]);
  not not_13 (not_13_out, in_1[2]);
  not not_14 (not_14_out, in_1[2]);
  not not_15 (not_15_out, in_1[0]);
  and and_1 (Jump, in_1[2], in_1[1], in_1[0]);
  and and_2 (RegDst, in_1[1], not_1_out);
  or or_1 (WrEn, not_2_out, not_3_out, not_4_out);
  and and_3 (and_3_out, not_5_out, in_1[1]);
  and and_4 (and_4_out, in_1[1], not_6_out);
  not not_16 (not_16_out, in_1[2]);
  and and_5 (and_5_out, in_1[1], not_7_out);
  and and_6 (out_5[0], in_1[2], not_8_out, in_1[0]);
  and and_7 (Sub, not_9_out, not_10_out, in_1[0]);
  and and_8 (le_enb, not_11_out, in_1[1], not_12_out);
  and and_9 (sw_enb, not_13_out, in_1[1], in_1[0]);
  and and_10 (RAM_to_Reg, not_14_out, in_1[1], not_15_out);
  or or_2 (Alu_Src, and_3_out, and_4_out);
  or or_3 (out_5[1], not_16_out, and_5_out);
endmodule
